# Fritzing sketch brazoRobotico (saved by Fritzing 0.9.3b)
breadboards: 2

parts:
  Part1 = Arduino Mega 2560 (Rev3)
  M1 = DC Motor
  M2 = DC Motor  # not connected
  M3 = DC Motor
  M4 = DC Motor  # not connected
  LED1 = LED - 5mm [color="Red (633nm)" package="5 mm [THT]"]
  LED2 = LED - 5mm [color="Green (565nm)" package="5 mm [THT]"]
  S1 = H-Bridge with L298N
  M5 = DC Motor  # not connected
  S2 = H-Bridge with L298N
  S3 = H-Bridge with L298N
  LCD1 = LCD screen
  J1 = Piezo Speaker
  S4 = Pushbutton [package=THT]
  R1 = Resistor [tolerance=±5% resistance=220 package="1206 [SMD]"]

nets:
  N1: Part1.D13_PWM, S1.IN1
  N2: Part1.D12_PWM, S1.IN2
  N3: Part1.D11_PWM, S3.IN1
  N4: Part1.D10_PWM, S3.IN2
  N5: Part1.D9_PWM, S2.IN1
  N6: Part1.D8_PWM, S2.IN2
  5V: Part1.5V, S1.5V, S2.5V, S3.5V, LCD1.VDD, LCD1.LED+, S4.leg0
  GND: Part1.GND, LED1.anode, LED2.anode, S1.GND, S2.GND, S3.GND, LCD1.VSS, LCD1.R/W, LCD1.LED-, J1.pin1, R1.Pin_0
  N7: Part1.D2_PWM, S1.IN4
  N8: Part1.D3_PWM, S1.IN3
  N9: Part1.D5_PWM, S4.leg1, R1.Pin_1
  N10: Part1.D6_PWM, S2.IN4
  N11: Part1.D7_PWM, S2.IN3
  N12: Part1.D22, LED2.cathode
  N13: Part1.D26, J1.pin2
  N14: Part1.D34, LCD1.DB7
  N15: Part1.D36, LCD1.DB6
  N16: Part1.D38, LCD1.DB5
  N17: Part1.D40, LCD1.DB4
  N18: Part1.D42, LCD1.E
  N19: Part1.D44, LCD1.RS
  N20: M1.pin_1, S1.OUT4-Motor2
  N21: M3.pin_1, S2.OUT4-Motor2

notes:
  base
  hombro
  codo
  muñeca
  pinza

custom parts:
  H-Bridge with L298N: h-bridge
